# Fritzing sketch schematic (saved by Fritzing 0.9.3b)

parts:
  Arduino1 = Arduino Mini (Rev5)
  Q1 = PNP-Transistor [package="SOT-23 [SMD]"]
  SP1 = SPEAKER [package=pcb_mount_speaker]
  S1 = Tilt Switch [package=THT]
  VCC1 = Battery block 9V
  R1 = Resistor [tolerance=±5% resistance=10k package="0603 [SMD]"]
  R2 = Resistor [tolerance=±5% resistance=1k package="0603 [SMD]"]

nets:
  N1: Arduino1.GND, SP1.+, VCC1.-, R1.Pin_0
  N2: Arduino1.5V, Q1.2, S1.Pin_2
  N3: Arduino1.A0, S1.Pin_1
  N4: Arduino1.D11_PWM, R2.Pin_1
  N5: Q1.1, SP1.-
